# Fritzing sketch DHT11 (saved by Fritzing 0.9.3b)
breadboards: 1

parts:
  Composant1 = Arduino Nano (Rev3.0)
  DHT1 = DHT11 Humitidy and Temperature Sensor
  Grove1 = Grove OLED 128x96
  LED1 = smd LED [color="Red (633nm)" package="1206 [SMD]"]

nets:
  GND: Composant1.GND, DHT1.NULL, DHT1.GND, Grove1.GND, LED1.cathode
  N1: Composant1.D2, LED1.anode
  N2: Composant1.D7, DHT1.VDD
  5V: Composant1.5V, DHT1.DATA, Grove1.VCC
  N3: Composant1.A5, Grove1.SCL
  N4: Composant1.A4, Grove1.SDA

custom parts:
  DHT11 Humitidy and Temperature Sensor: DHT11 Humidity and Temperature Sensor
